// Logisim project ROFIQUL ALAM SHEHAB_1831185042.circ as structural Verilog
module AND_IC (
  input  in_1,
  input  in_2,
  input  in_3,
  input  in_4,
  input  in_5,
  input  in_6,
  input  in_7,
  input  in_8,
  input  in_9,
  input  in_10,
  output out_11,
  output out_12,
  output out_13,
  output out_14
);

  and and_1 (out_11, in_2, in_3);
  and and_2 (out_12, in_4, in_5);
  and and_3 (out_13, in_6, in_7);
  and and_4 (out_14, in_8, in_9);
endmodule

module OR_IC (
  input  in_1,
  input  in_2,
  input  in_3,
  input  in_4,
  input  in_5,
  input  in_6,
  input  in_7,
  input  in_8,
  input  in_9,
  input  in_10,
  output out_11,
  output out_12,
  output out_13,
  output out_14
);

  or or_1 (out_11, in_2, in_3);
  or or_2 (out_12, in_4, in_5);
  or or_3 (out_13, in_6, in_7);
  or or_4 (out_14, in_8, in_9);
endmodule

module XOR_IC (
  input  in_1,
  input  in_2,
  input  in_3,
  input  in_4,
  input  in_5,
  input  in_6,
  input  in_7,
  input  in_8,
  input  in_9,
  input  in_10,
  output out_11,
  output out_12,
  output out_13,
  output out_14
);

  xor xor_1 (out_11, in_2, in_3);
  xor xor_2 (out_12, in_4, in_5);
  xor xor_3 (out_13, in_6, in_7);
  xor xor_4 (out_14, in_8, in_9);
endmodule

module _4_1_MUX_IC (
  input  in_1,
  input  in_2,
  input  in_3,
  input  in_4,
  input  in_5,
  input  in_6,
  output out_7
);

  wire and_1_out, and_2_out, and_3_out, and_4_out, not_1_out, not_2_out;

  not not_1 (not_1_out, in_5);
  not not_2 (not_2_out, in_6);
  and and_1 (and_1_out, in_1, not_2_out, not_1_out);
  and and_2 (and_2_out, in_2, not_1_out, in_6);
  and and_3 (and_3_out, in_3, not_2_out, in_5);
  and and_4 (and_4_out, in_4, in_5, in_6);
  or or_1 (out_7, and_1_out, and_2_out, and_3_out, and_4_out);
endmodule

module NOT_IC (
  input  in_1,
  input  in_2,
  input  in_3,
  input  in_4,
  input  in_5,
  input  in_6,
  input  in_7,
  input  in_8,
  output out_9,
  output out_10,
  output out_11,
  output out_12,
  output out_13,
  output out_14
);


  assign out_9 = in_2;
  assign out_10 = in_3;
  assign out_11 = in_4;
  assign out_12 = in_5;
  assign out_13 = in_6;
  assign out_14 = in_7;
endmodule

module _2_BIT_LOGIC_UNIT (
  input  A1,
  input  B1,
  input  A2,
  input  B2,
  input  in_5,
  input  in_6,
  output out_7,
  output out_8
);

  wire and_ic_1_out_11, and_ic_1_out_12, not_ic_1_out_9, not_ic_1_out_10, or_ic_1_out_11, or_ic_1_out_12,
       xor_ic_1_out_11, xor_ic_1_out_12;

  AND_IC and_ic_1 (
    .in_2(A1), .in_3(B1), .in_4(A2), .in_5(B2), .out_11(and_ic_1_out_11), .out_12(and_ic_1_out_12));  // open: in_6, in_7, in_8, in_9, out_13, out_14, in_1, in_10
  OR_IC or_ic_1 (
    .in_2(A1), .in_3(B1), .in_4(A2), .in_5(B2), .out_11(or_ic_1_out_11), .out_12(or_ic_1_out_12));  // open: in_1, in_6, in_7, in_8, in_9, in_10, out_13, out_14
  XOR_IC xor_ic_1 (
    .in_2(A1), .in_3(B1), .in_4(A2), .in_5(B2), .out_11(xor_ic_1_out_11), .out_12(xor_ic_1_out_12));  // open: in_1, in_6, in_7, in_8, in_9, in_10, out_13, out_14
  NOT_IC not_ic_1 (
    .in_2(A1), .in_3(A2), .out_9(not_ic_1_out_9), .out_10(not_ic_1_out_10));  // open: in_1, in_4, in_5, in_6, in_7, in_8, out_11, out_12, out_13, out_14
  _4_1_MUX_IC u_4_1_mux_ic_1 (
    .in_1(and_ic_1_out_11), .in_2(or_ic_1_out_11), .in_3(xor_ic_1_out_11), .in_4(not_ic_1_out_9),
    .in_5(in_5), .in_6(in_6), .out_7(out_7));
  _4_1_MUX_IC u_4_1_mux_ic_2 (
    .in_1(and_ic_1_out_12), .in_2(or_ic_1_out_12), .in_3(xor_ic_1_out_12), .in_4(not_ic_1_out_10),
    .in_5(in_5), .in_6(in_6), .out_7(out_8));
endmodule

module _4_BIT_ADDER (
  input  in_1,
  input  C,
  input  S4,
  input  S3,
  input  S2,
  input  S1,
  input  B4,
  input  B3,
  input  B2,
  input  B1,
  input  A4,
  input  A3,
  input  A2,
  input  A1
);

  wire and_1_out, and_2_out, and_3_out, and_4_out, and_5_out, and_6_out, and_7_out, and_8_out, xor_1_out,
       xor_2_out, xor_3_out, xor_4_out, xor_9_out, xor_10_out, xor_11_out;

  xor xor_1 (xor_1_out, A1, B1);
  and and_1 (and_1_out, A1, B1);
  xor xor_2 (xor_2_out, A2, B2);
  and and_2 (and_2_out, A2, B2);
  xor xor_3 (xor_3_out, A3, B3);
  and and_3 (and_3_out, A3, B3);
  xor xor_4 (xor_4_out, A4, B4);
  and and_4 (and_4_out, A4, B4);
  xor xor_5 (S1, xor_1_out, in_1);
  and and_5 (and_5_out, xor_1_out, in_1);
  xor xor_6 (S2, xor_2_out, xor_9_out);
  and and_6 (and_6_out, xor_2_out, xor_9_out);
  xor xor_7 (S3, xor_3_out, xor_10_out);
  and and_7 (and_7_out, xor_3_out, xor_10_out);
  xor xor_8 (S4, xor_4_out, xor_11_out);
  and and_8 (and_8_out, xor_4_out, xor_11_out);
  xor xor_9 (xor_9_out, and_5_out, and_1_out);
  xor xor_10 (xor_10_out, and_6_out, and_2_out);
  xor xor_11 (xor_11_out, and_7_out, and_3_out);
  xor xor_12 (C, and_8_out, and_4_out);
endmodule

module D_FLIP_FLOP (
  input  SET,
  input  CLICK,
  input  DATA,
  input  RESET,
  output out_5,
  output out_6
);

  wire nand_1_out, nand_2_out, nand_3_out, nand_4_out, not_1_out, not_2_out;

  not not_1 (not_1_out, SET);
  not not_2 (not_2_out, RESET);
  nand nand_1 (nand_1_out, not_1_out, nand_4_out, nand_2_out);
  nand nand_2 (nand_2_out, nand_1_out, CLICK, not_2_out);
  nand nand_3 (nand_3_out, nand_2_out, CLICK, nand_4_out);
  nand nand_4 (nand_4_out, nand_3_out, DATA, not_2_out);
  nand nand_5 (out_5, not_1_out, nand_2_out, out_6);
  nand nand_6 (out_6, out_5, nand_3_out, not_2_out);

  // Notes on the sheet:
  //   D-FLIP_FLOP
endmodule

module _2_BIT_LOGIC_UNIT_LOG (
  input  A1,
  input  B2,
  input  A2,
  input  B2_2,
  input  [1:0] S1_S2,
  output out_6,
  output out_7
);

  wire and_1_out, and_2_out, not_1_out, not_2_out, or_1_out, or_2_out, xor_1_out, xor_2_out;

  and and_1 (and_1_out, A1, B2);
  or or_1 (or_1_out, A1, B2);
  xor xor_1 (xor_1_out, A1, B2);
  not not_1 (not_1_out, A1);
  and and_2 (and_2_out, A2, B2_2);
  or or_2 (or_2_out, A2, B2_2);
  xor xor_2 (xor_2_out, A2, B2_2);
  not not_2 (not_2_out, A2);
  Multiplexer #(.select(2)) multiplexer_1 (
    .in0(and_1_out), .in1(or_1_out), .in2(xor_1_out), .in3(not_1_out), .out(out_6), .sel(S1_S2));  // open: en
  Multiplexer #(.select(2)) multiplexer_2 (
    .in0(and_2_out), .in1(or_2_out), .in2(xor_2_out), .in3(not_2_out), .out(out_7), .sel(S1_S2));  // open: en

  // Notes on the sheet:
  //   2-BIT_LOGIC_UNIT
endmodule
